# Fritzing sketch Untitled Sketch (saved by Fritzing 0.9.3b)
breadboards: 1

parts:
  Raspberry_Pi_1 = Raspberry Pi 3 [part_number=RPI-3-V1.2]
  DS1 = DS18B20 1-Wire Temperature Sensor [part_number=DS18B20]
  R1 = Resistor [tolerance=±5% resistance=1k package="2512 [SMD]"]
  M1 = DC Motor
  U2 = RELAY [package=relay-t9a]
  V1 = DC Power [voltage=5]
  Q1 = PNP-Transistor [package="TO92 [THT]"]
  Fuse2 = Fuse with Handler [part_number=Htc-15m]
  V2 = DC Power [voltage=5]
  Q2 = PNP-Transistor [package="TO92 [THT]"]
  LED1 = LED - 5mm [color="Red (633nm)" package="5 mm [THT]"]
  U3 = RELAY [package=relay-t9a]
  Fuse3 = Fuse with Handler [part_number=Htc-15m]
  Power_plug1 = Power plug
  Power_plug2 = Power plug
  R2 = Resistor [tolerance=±5% resistance=220 package=THT]
  R3 = Resistor [tolerance=±5% resistance=220 package=THT]

nets:
  N1: Raspberry_Pi_1.GPIO4, Q2.B, R2.Pin_0
  GND: Raspberry_Pi_1.GND, DS1.GND, R2.Pin_1, R3.Pin_0
  N2: Raspberry_Pi_1.GPIO21, DS1.DQ, R1.Pin_1
  N3: Raspberry_Pi_1.GPIO18, Q1.B, R3.Pin_1
  5V: Raspberry_Pi_1.5V, DS1.VDD, R1.Pin_0
  N4: M1.pin_1, U2.NC
  N5: M1.pin_2, Fuse2.Connector1
  N6: U2.COIL1, V1.V-
  N7: U2.MAIN, Power_plug2.GND
  N8: V1.V+, Q1.E
  N9: Fuse2.Connector2, Power_plug2.VCC
  N10: V2.V+, Q2.E
  N11: V2.V-, U3.COIL1
  N12: Q2.C, U3.COIL2
  N13: LED1.cathode, Fuse3.Connector2
  N14: LED1.anode, U3.NO
  N15: U3.MAIN, Power_plug1.VCC
  N16: Fuse3.Connector1, Power_plug1.GND
